# Fritzing sketch schema_panneau (saved by Fritzing 0.8.0b)
breadboards: 1

parts:
  LED1 = RGB LED (com. anode, rbg) [package="5 mm [THT]"]
  R3 = Resistor [tolerance=±5% resistance=330 package=THT]
  R4 = Resistor [tolerance=±5% resistance=330 package=THT]
  R5 = Resistor [tolerance=±5% resistance=220 package=THT]
  LED2 = LED - 5mm [color="White (8000K)" package="5 mm [THT]"]
  R8 = Resistor [tolerance=±5% resistance=220 package=THT]
  J1 = Peltier Element
  J2 = Peltier Element
  Arduino_Ethernet_Shield1 = Arduino Ethernet Shield
  S1 = Pushbutton [package="[THT]"]
  R9 = Resistor [tolerance=±5% resistance=10k package=THT]
  R10 = Resistor [tolerance=±5% resistance=10k package=THT]
  R11 = Resistor [tolerance=±5% resistance=10k package=THT]
  R15 = Resistor [tolerance=±5% resistance=10k package=THT]
  S3 = Pushbutton [package="[THT]"]
  S4 = Pushbutton [package="[THT]"]
  S5 = Pushbutton [package="[THT]"]
  S6 = Toggle Switch [package=THT]
  R19 = Resistor [tolerance=±5% resistance=220 package=THT]

nets:
  N1: LED1.red_cathode, R5.Pin_1
  N2: LED1.blue_cathode, R3.Pin_1
  N3: LED1.green_cathode, R4.Pin_1
  N4: R3.Pin_0, Arduino_Ethernet_Shield1.MOSI
  N5: R4.Pin_0, Arduino_Ethernet_Shield1.SS#5
  N6: R5.Pin_0, Arduino_Ethernet_Shield1.SCK
  N7: LED2.cathode, Arduino_Ethernet_Shield1.D9
  N8: LED2.anode, R8.Pin_1
  N9: R8.Pin_0, Arduino_Ethernet_Shield1.+5V, R9.Pin_1, R10.Pin_1, R11.Pin_0, R15.Pin_0
  N10: J1.pin2, Arduino_Ethernet_Shield1.D6
  N11: J2.pin1, Arduino_Ethernet_Shield1.GND, S1.Pin_3, S1.Pin_4, S3.Pin_3, S3.Pin_4, S4.Pin_3, S4.Pin_4, S5.Pin_3, S5.Pin_4, S6.L2
  N12: J2.pin2, Arduino_Ethernet_Shield1.D5
  N13: Arduino_Ethernet_Shield1.MISO, S1.Pin_1, R10.Pin_0
  N14: Arduino_Ethernet_Shield1.D8, R15.Pin_1, S5.Pin_1, S5.Pin_2
  N15: Arduino_Ethernet_Shield1.D7, R9.Pin_0, S3.Pin_1, S3.Pin_2
  N16: Arduino_Ethernet_Shield1.SS#11, R11.Pin_1, S4.Pin_1, S4.Pin_2
  N17: Arduino_Ethernet_Shield1.D2, S6.COM
  N18: S6.L1, R19.Pin_1

notes:
  2 x Galvanomètres avec resistance 2kΩ en parallèle (pour que la plage d'affichage aille de 0 à 5V)
  Levier de gauche 3 positions (middle off, right pos. and left pos,
  Levier de droite 3 positions (middle off, right pos. and left pos,
  LEDs
  - une Red
  - une RGB
